// Logisim project realAlu.circ as structural Verilog
module AND (
  input  [7:0] A,
  input  E,
  input  [7:0] B,
  output out_4,
  output [7:0] out_5
);

  wire [7:0] bit_extender_1_out;

  assign bit_extender_1_out = {{7{E}}, E};  // Bit_Extender bit_extender_1
  flag_z flag_z_1 (.in_1(out_5), .out_2(out_4));
  assign out_5 = A & bit_extender_1_out & B;  // AND_Gate and_1, 8 bits wide
endmodule

module OR (
  input  E,
  input  [7:0] A,
  input  [7:0] B,
  output out_4,
  output [7:0] out_5
);

  wire [7:0] bit_extender_1_out, or_1_out;

  assign or_1_out = A | B;  // OR_Gate or_1, 8 bits wide
  assign bit_extender_1_out = {{7{E}}, E};  // Bit_Extender bit_extender_1
  flag_z flag_z_1 (.in_1(out_5), .out_2(out_4));
  assign out_5 = bit_extender_1_out & or_1_out;  // AND_Gate and_1, 8 bits wide
endmodule

module HA (
  input  in_1,
  input  in_2,
  output out_3,
  output out_4
);

  xor xor_1 (out_3, in_2, in_1);
  and and_1 (out_4, in_2, in_1);
endmodule

module FA (
  input  in_1,
  input  in_2,
  input  in_3,
  output out_4,
  output out_5
);

  wire and_1_out, and_2_out, and_3_out, xor_1_out;

  and and_1 (and_1_out, in_3, in_2);
  and and_2 (and_2_out, in_3, in_1);
  and and_3 (and_3_out, in_2, in_1);
  xor xor_1 (xor_1_out, in_3, in_2);
  xor xor_2 (out_4, xor_1_out, in_1);
  or or_1 (out_5, and_1_out, and_2_out, and_3_out);
endmodule

module Adder_4bits (
  input  in_1,
  input  in_2,
  input  in_3,
  input  in_4,
  input  in_5,
  input  in_6,
  input  in_7,
  input  in_8,
  input  in_9,
  output out_10,
  output out_11,
  output out_12,
  output out_13,
  output out_14
);

  wire fa_1_out_5, fa_2_out_5, fa_3_out_5;

  FA fa_1 (.out_4(out_10), .out_5(fa_1_out_5), .in_1(in_3), .in_2(in_2), .in_3(in_1));
  FA fa_2 (.out_4(out_11), .out_5(fa_2_out_5), .in_1(fa_1_out_5), .in_2(in_5), .in_3(in_4));
  FA fa_3 (.out_4(out_12), .out_5(fa_3_out_5), .in_1(fa_2_out_5), .in_2(in_7), .in_3(in_6));
  FA fa_4 (.out_4(out_13), .out_5(out_14), .in_1(fa_3_out_5), .in_2(in_9), .in_3(in_8));
endmodule

module Adder_8_bits (
  input  in_1,
  input  in_2,
  input  in_3,
  input  in_4,
  input  in_5,
  input  in_6,
  input  in_7,
  input  in_8,
  input  in_9,
  input  in_10,
  input  in_11,
  input  in_12,
  input  in_13,
  input  in_14,
  input  in_15,
  input  in_16,
  input  in_17,
  output out_18,
  output [7:0] out_19
);

  wire adder_4bits_2_out_14;
  wire [7:0] adder_4bits_2_out_10, bit_extender_1_out;

  Adder_4bits adder_4bits_1 (
    .out_10(adder_4bits_2_out_10[4]), .out_11(adder_4bits_2_out_10[5]), .out_12(adder_4bits_2_out_10[6]),
    .out_13(adder_4bits_2_out_10[7]), .in_1(in_7), .in_4(in_5), .in_6(in_3), .in_8(in_1), .in_2(in_8),
    .in_5(in_6), .in_7(in_4), .in_9(in_2), .in_3(adder_4bits_2_out_14), .out_14(out_18));
  assign out_19 = adder_4bits_2_out_10 & bit_extender_1_out;  // AND_Gate and_1, 8 bits wide
  Adder_4bits adder_4bits_2 (
    .out_10(adder_4bits_2_out_10[0]), .out_11(adder_4bits_2_out_10[1]), .out_12(adder_4bits_2_out_10[2]),
    .out_13(adder_4bits_2_out_10[3]), .in_1(in_15), .in_4(in_13), .in_6(in_11), .in_8(in_9), .in_2(in_16),
    .in_5(in_14), .in_7(in_12), .in_9(in_10), .in_3(1'b0), .out_14(adder_4bits_2_out_14));
  assign bit_extender_1_out = {{7{in_17}}, in_17};  // Bit_Extender bit_extender_1
endmodule

module NOT_B (
  input  E,
  input  [7:0] B,
  output out_3,
  output [7:0] out_4
);

  wire [7:0] bit_extender_1_out, not_1_out;

  assign bit_extender_1_out = {{7{E}}, E};  // Bit_Extender bit_extender_1
  assign not_1_out = ~B;  // NOT_Gate not_1, 8 bits wide
  assign out_4 = bit_extender_1_out & not_1_out;  // AND_Gate and_1, 8 bits wide
  flag_z flag_z_1 (.in_1(out_4), .out_2(out_3));
endmodule

module LSL_B (
  input  [7:0] B,
  input  e,
  output out_3,
  output out_4,
  output [7:0] out_5
);

  wire [6:0] bit_extender_1_out;

  assign out_5[7:1] = B[6:0] & bit_extender_1_out;  // AND_Gate and_1, 7 bits wide
  assign bit_extender_1_out = {{6{e}}, e};  // Bit_Extender bit_extender_1
  flag_z flag_z_1 (.in_1({out_5[7:1], 1'b0}), .out_2(out_3));

  assign out_4 = B[7];
  assign out_5[0] = 1'b0;
endmodule

module CPL_2 (
  input  in_1,
  input  [7:0] in_2,
  output C,
  output [7:0] out_4
);

  wire ha_1_out_4, ha_2_out_4, ha_3_out_4, ha_4_out_4, ha_5_out_4, ha_6_out_4, ha_8_out_4;
  wire [7:0] bit_extender_1_out, ha_1_out_3, not_1_out;

  // Probe on in_2
  assign not_1_out = ~in_2;  // NOT_Gate not_1, 8 bits wide
  HA ha_1 (.out_3(ha_1_out_3[0]), .out_4(ha_1_out_4), .in_1(1'b1), .in_2(not_1_out[0]));
  HA ha_2 (.out_3(ha_1_out_3[3]), .out_4(ha_2_out_4), .in_1(not_1_out[3]), .in_2(ha_3_out_4));
  HA ha_3 (.out_3(ha_1_out_3[2]), .out_4(ha_3_out_4), .in_1(not_1_out[2]), .in_2(ha_4_out_4));
  HA ha_4 (.out_3(ha_1_out_3[1]), .out_4(ha_4_out_4), .in_1(not_1_out[1]), .in_2(ha_1_out_4));
  HA ha_5 (.out_3(ha_1_out_3[5]), .out_4(ha_5_out_4), .in_1(not_1_out[5]), .in_2(ha_6_out_4));
  HA ha_6 (.out_3(ha_1_out_3[4]), .out_4(ha_6_out_4), .in_1(not_1_out[4]), .in_2(ha_2_out_4));
  HA ha_7 (.out_3(ha_1_out_3[7]), .out_4(C), .in_1(not_1_out[7]), .in_2(ha_8_out_4));
  HA ha_8 (.out_3(ha_1_out_3[6]), .out_4(ha_8_out_4), .in_1(not_1_out[6]), .in_2(ha_5_out_4));
  assign bit_extender_1_out = {{7{in_1}}, in_1};  // Bit_Extender bit_extender_1
  assign out_4 = bit_extender_1_out & ha_1_out_3;  // AND_Gate and_1, 8 bits wide
endmodule

module Sottrattore (
  input  in_1,
  input  [7:0] B,
  input  [7:0] A,
  input  in_4,
  output [7:0] out_5,
  output out_6,
  output out_7
);

  wire cpl_2_1_c;
  wire [7:0] cpl_2_1_out_4;

  // Probe on B
  CPL_2 cpl_2_1 (.in_2(B), .C(cpl_2_1_c), .out_4(cpl_2_1_out_4), .in_1(in_1));
  // Probe on A
  LED led_1 (.in(cpl_2_1_c));
  Adder_8_bits adder_8_bits_1 (
    .in_2(A[7]), .in_4(A[6]), .in_6(A[5]), .in_8(A[4]), .in_10(A[3]), .in_12(A[2]), .in_14(A[1]),
    .in_16(A[0]), .in_1(cpl_2_1_out_4[7]), .in_3(cpl_2_1_out_4[6]), .in_5(cpl_2_1_out_4[5]),
    .in_7(cpl_2_1_out_4[4]), .in_9(cpl_2_1_out_4[3]), .in_11(cpl_2_1_out_4[2]), .in_13(cpl_2_1_out_4[1]),
    .in_15(cpl_2_1_out_4[0]), .out_18(out_7), .in_17(in_4), .out_19(out_5));
  // Probe on out_5
  flag_z flag_z_1 (.in_1(out_5), .out_2(out_6));
endmodule

module LSR_B (
  input  [7:0] in_1,
  input  E,
  output out_3,
  output out_4,
  output [7:0] out_5
);

  wire [6:0] bit_extender_1_out;

  assign bit_extender_1_out = {{6{E}}, E};  // Bit_Extender bit_extender_1
  assign out_5[6:0] = in_1[7:1] & bit_extender_1_out;  // AND_Gate and_1, 7 bits wide
  flag_z flag_z_1 (.in_1({1'b0, out_5[6:0]}), .out_2(out_3));

  assign out_4 = in_1[0];
  assign out_5[7] = 1'b0;
endmodule

module INC_B (
  input  in_1,
  input  in_2,
  input  in_3,
  input  in_4,
  input  in_5,
  input  in_6,
  input  in_7,
  input  in_8,
  input  in_9,
  output out_10,
  output out_11,
  output out_12,
  output out_13,
  output out_14,
  output out_15,
  output out_16,
  output out_17
);

  wire fa_1_out_4, fa_1_out_5, fa_2_out_4, fa_2_out_5, fa_3_out_4, fa_3_out_5, fa_4_out_4, fa_4_out_5,
       fa_5_out_4, fa_5_out_5, fa_6_out_4, fa_6_out_5, fa_7_out_4, fa_7_out_5, fa_8_out_4;

  FA fa_1 (.out_4(fa_1_out_4), .out_5(fa_1_out_5), .in_1(1'b0), .in_2(in_1), .in_3(1'b1));
  FA fa_2 (.out_4(fa_2_out_4), .out_5(fa_2_out_5), .in_1(fa_1_out_5), .in_2(in_2), .in_3(1'b0));
  FA fa_3 (.out_4(fa_3_out_4), .out_5(fa_3_out_5), .in_1(fa_2_out_5), .in_2(in_3), .in_3(1'b0));
  FA fa_4 (.out_4(fa_4_out_4), .out_5(fa_4_out_5), .in_1(fa_3_out_5), .in_2(in_4), .in_3(1'b0));
  FA fa_5 (.out_4(fa_5_out_4), .out_5(fa_5_out_5), .in_1(fa_4_out_5), .in_2(in_6), .in_3(1'b0));
  FA fa_6 (.out_4(fa_6_out_4), .out_5(fa_6_out_5), .in_1(fa_5_out_5), .in_2(in_7), .in_3(1'b0));
  FA fa_7 (.out_4(fa_7_out_4), .out_5(fa_7_out_5), .in_1(fa_6_out_5), .in_2(in_8), .in_3(1'b0));
  FA fa_8 (.out_4(fa_8_out_4), .in_1(fa_7_out_5), .in_2(in_9), .in_3(1'b0));  // open: out_5
  and and_1 (out_17, fa_1_out_4, in_5);
  and and_2 (out_16, fa_2_out_4, in_5);
  and and_3 (out_15, fa_3_out_4, in_5);
  and and_4 (out_14, fa_4_out_4, in_5);
  and and_5 (out_13, fa_5_out_4, in_5);
  and and_6 (out_12, fa_6_out_4, in_5);
  and and_7 (out_11, fa_7_out_4, in_5);
  and and_8 (out_10, fa_8_out_4, in_5);
endmodule

module DEC_B (
  input  in_1,
  input  in_2,
  input  in_3,
  input  in_4,
  input  in_5,
  input  in_6,
  input  in_7,
  input  in_8,
  input  in_9,
  output out_10,
  output out_11,
  output out_12,
  output out_13,
  output out_14,
  output out_15,
  output out_16,
  output out_17,
  output out_18
);

  wire fa_1_out_4, fa_1_out_5, fa_2_out_4, fa_2_out_5, fa_3_out_4, fa_3_out_5, fa_4_out_4, fa_4_out_5,
       fa_5_out_4, fa_5_out_5, fa_6_out_4, fa_6_out_5, fa_7_out_4, fa_7_out_5, fa_8_out_4;

  FA fa_1 (.out_4(fa_1_out_4), .out_5(fa_1_out_5), .in_1(in_5), .in_2(1'b0), .in_3(in_1));
  FA fa_2 (.out_4(fa_2_out_4), .out_5(fa_2_out_5), .in_1(fa_1_out_5), .in_2(1'b1), .in_3(in_2));
  FA fa_3 (.out_4(fa_3_out_4), .out_5(fa_3_out_5), .in_1(fa_2_out_5), .in_2(1'b1), .in_3(in_3));
  FA fa_4 (.out_4(fa_4_out_4), .out_5(fa_4_out_5), .in_1(fa_3_out_5), .in_2(1'b1), .in_3(in_4));
  FA fa_5 (.out_4(fa_5_out_4), .out_5(fa_5_out_5), .in_1(fa_4_out_5), .in_2(1'b1), .in_3(in_6));
  FA fa_6 (.out_4(fa_6_out_4), .out_5(fa_6_out_5), .in_1(fa_5_out_5), .in_2(1'b1), .in_3(in_7));
  FA fa_7 (.out_4(fa_7_out_4), .out_5(fa_7_out_5), .in_1(fa_6_out_5), .in_2(1'b1), .in_3(in_8));
  FA fa_8 (.out_4(fa_8_out_4), .out_5(out_18), .in_1(fa_7_out_5), .in_2(1'b1), .in_3(in_9));
  and and_1 (out_10, in_5, fa_1_out_4);
  and and_2 (out_11, in_5, fa_2_out_4);
  and and_3 (out_12, in_5, fa_3_out_4);
  and and_4 (out_13, in_5, fa_4_out_4);
  and and_5 (out_14, in_5, fa_5_out_4);
  and and_6 (out_15, in_5, fa_6_out_4);
  and and_7 (out_16, in_5, fa_7_out_4);
  and and_8 (out_17, in_5, fa_8_out_4);
endmodule

module DECODER (
  input  in_1,
  input  in_2,
  input  in_3,
  input  in_4,
  output out_5,
  output out_6,
  output out_7,
  output out_8,
  output out_9,
  output out_10,
  output out_11,
  output out_12,
  output out_13,
  output out_14
);

  wire not_1_out, not_2_out, not_3_out, not_4_out;

  not not_1 (not_1_out, in_1);
  not not_2 (not_2_out, in_3);
  not not_3 (not_3_out, in_2);
  not not_4 (not_4_out, in_4);
  and and_1 (out_5, not_1_out, not_3_out, not_2_out, not_4_out);
  and and_2 (out_6, not_1_out, not_3_out, not_2_out, in_4);
  and and_3 (out_7, not_1_out, not_3_out, in_3, not_4_out);
  and and_4 (out_8, not_1_out, not_3_out, in_3, in_4);
  and and_5 (out_9, not_1_out, in_2, not_2_out, not_4_out);
  and and_6 (out_10, not_1_out, in_2, not_2_out, in_4);
  and and_7 (out_11, not_1_out, in_2, in_3, not_4_out);
  and and_8 (out_12, not_1_out, in_2, in_3, in_4);
  and and_9 (out_13, in_1, not_3_out, not_2_out, not_4_out);
  and and_10 (out_14, in_1, not_3_out, not_2_out, in_4);
endmodule

module Tutto_insieme (
  input  [7:0] in_1,
  input  [7:0] in_2,
  input  in_3,
  input  in_4,
  input  in_5,
  input  in_6,
  output [7:0] out_7,
  output out_8
);

  wire decoder_1_out_5, decoder_1_out_6, decoder_1_out_7, decoder_1_out_8, decoder_1_out_9, decoder_1_out_10,
       decoder_1_out_11, decoder_1_out_12, decoder_1_out_13, decoder_1_out_14, lsr_b_1_out_3, z0, z1, z2, z3,
       z4, z5, z6, z7;
  wire [7:0] adder_finito_1_out_5, and_1_out_5, dec_finito_1_out_4, inc_finito_1_out_3, input_a_1_out_4,
       lsl_b_1_out_5, lsr_b_1_out_5, not_b_1_out_4, or_1_out_5, sottrattore_1_out_5;

  nor nor_1 (out_8, z0, z1, z2, z3, z4, z5, z6, z7);
  DECODER decoder_1 (
    .in_1(in_3), .in_2(in_4), .in_3(in_5), .in_4(in_6), .out_5(decoder_1_out_5), .out_6(decoder_1_out_6),
    .out_7(decoder_1_out_7), .out_8(decoder_1_out_8), .out_9(decoder_1_out_9), .out_10(decoder_1_out_10),
    .out_11(decoder_1_out_11), .out_12(decoder_1_out_12), .out_13(decoder_1_out_13), .out_14(decoder_1_out_14));
  AND and_1 (.A(in_1), .B(in_2), .out_5(and_1_out_5), .E(decoder_1_out_5), .out_4(z0));
  OR or_1 (.A(in_1), .B(in_2), .E(decoder_1_out_6), .out_5(or_1_out_5), .out_4(z1));
  NOT_B not_b_1 (.B(in_2), .out_4(not_b_1_out_4), .E(decoder_1_out_7), .out_3(z2));
  LSL_B lsl_b_1 (.B(in_2), .out_5(lsl_b_1_out_5), .e(decoder_1_out_8), .out_3(z3));  // open: out_4
  LSR_B lsr_b_1 (.in_1(in_2), .out_5(lsr_b_1_out_5), .E(decoder_1_out_9), .out_3(lsr_b_1_out_3));  // open: out_4
  input_A input_a_1 (.in_1(decoder_1_out_14), .in_2(in_1), .out_4(input_a_1_out_4), .out_3(z7));
  adder_finito adder_finito_1 (
    .in_1(in_2), .in_2(in_1), .in_3(decoder_1_out_10), .out_5(adder_finito_1_out_5), .out_4(z4));  // open: out_6
  Sottrattore sottrattore_1 (
    .B(in_2), .A(in_1), .out_5(sottrattore_1_out_5), .in_4(decoder_1_out_11), .in_1(1'b1), .out_6(z5));  // open: out_7
  inc_finito inc_finito_1 (.in_1(in_2), .out_3(inc_finito_1_out_3), .in_2(decoder_1_out_12), .out_4(z6));
  dec_finito dec_finito_1 (.in_1(in_2), .out_4(dec_finito_1_out_4), .in_2(decoder_1_out_13));  // open: out_5, out_3
  assign out_7 = and_1_out_5 | or_1_out_5 | not_b_1_out_4 | lsl_b_1_out_5 | lsr_b_1_out_5 | adder_finito_1_out_5 | sottrattore_1_out_5 | inc_finito_1_out_3 | dec_finito_1_out_4 | input_a_1_out_4;  // OR_Gate or_2, 8 bits wide

  // Other names for the same wires on the sheet: A[7:0] = in_1; B[7:0] = in_2
endmodule

module adder_finito (
  input  [7:0] in_1,
  input  [7:0] in_2,
  input  in_3,
  output out_4,
  output [7:0] out_5,
  output out_6
);

  Adder_8_bits adder_8_bits_1 (
    .in_2(in_2[7]), .in_4(in_2[6]), .in_6(in_2[5]), .in_8(in_2[4]), .in_10(in_2[3]), .in_12(in_2[2]),
    .in_14(in_2[1]), .in_16(in_2[0]), .in_1(in_1[7]), .in_3(in_1[6]), .in_5(in_1[5]), .in_7(in_1[4]),
    .in_9(in_1[3]), .in_11(in_1[2]), .in_13(in_1[1]), .in_15(in_1[0]), .out_18(out_6), .in_17(in_3),
    .out_19(out_5));
  flag_z flag_z_1 (.in_1(out_5), .out_2(out_4));
endmodule

module inc_finito (
  input  [7:0] in_1,
  input  in_2,
  output [7:0] out_3,
  output out_4
);

  INC_B inc_b_1 (
    .in_1(in_1[0]), .in_2(in_1[1]), .in_3(in_1[2]), .in_4(in_1[3]), .in_5(in_2), .in_6(in_1[4]),
    .in_7(in_1[5]), .in_8(in_1[6]), .in_9(in_1[7]), .out_10(out_3[7]), .out_11(out_3[6]), .out_12(out_3[5]),
    .out_13(out_3[4]), .out_14(out_3[3]), .out_15(out_3[2]), .out_16(out_3[1]), .out_17(out_3[0]));
  flag_z flag_z_1 (.in_1(out_3), .out_2(out_4));
endmodule

module dec_finito (
  input  [7:0] in_1,
  input  in_2,
  output out_3,
  output [7:0] out_4,
  output out_5
);

  DEC_B dec_b_1 (
    .in_1(in_1[0]), .in_2(in_1[1]), .in_3(in_1[2]), .in_4(in_1[3]), .in_5(in_2), .in_6(in_1[4]),
    .in_7(in_1[5]), .in_8(in_1[6]), .in_9(in_1[7]), .out_10(out_4[0]), .out_11(out_4[1]), .out_12(out_4[2]),
    .out_13(out_4[3]), .out_14(out_4[4]), .out_15(out_4[5]), .out_16(out_4[6]), .out_17(out_4[7]),
    .out_18(out_5));
  flag_z flag_z_1 (.in_1(out_4), .out_2(out_3));
endmodule

module input_A (
  input  in_1,
  input  [7:0] in_2,
  output out_3,
  output [7:0] out_4
);

  wire [7:0] bit_extender_1_out;

  assign bit_extender_1_out = {{7{in_1}}, in_1};  // Bit_Extender bit_extender_1
  assign out_4 = bit_extender_1_out & in_2;  // AND_Gate and_1, 8 bits wide
  flag_z flag_z_1 (.in_1(out_4), .out_2(out_3));
endmodule

module flag_z (
  input  [7:0] in_1,
  output out_2
);

  nor nor_1 (out_2, in_1[0], in_1[1], in_1[2], in_1[3], in_1[4], in_1[5], in_1[6], in_1[7]);
endmodule
